# Fritzing sketch tiny (saved by Fritzing 0.9.2b)
breadboards: 1

parts:
  U1 = NodeMCU
  U2 = attiny85 [package=dip]
  S1 = Pushbutton [package="[SMD]"]
  LED1 = LED - 3mm [color="Red (633nm)" package="3 mm [THT]"]
  LED2 = LED - 3mm [color="Green (560nm)" package="3 mm [THT]"]
  U3 = Battery Holders [package=battery-aaa]
  U4 = Battery Holders [package=battery-aaa]
  U5 = Battery Holders [package=battery-aaa]

nets:
  N1: U1.connector11, U2.Pin_5, LED1.cathode, LED2.anode
  N2: U1.connector12, U2.Pin_6, LED1.anode, LED2.cathode
  N3: U1.connector15, U2.Pin_8, U3.+
  N4: U1.connector16, U2.Pin_4, U2.Pin_7, S1.Pin_1, S1.Pin_2, S1.Pin_3, S1.Pin_4, U5.-
  N5: U3.-, U4.+
  N6: U4.-, U5.+
